# Fritzing sketch Totobot (saved by Fritzing 0.9.3b)
breadboards: 1

parts:
  Module_1 = Arduino Uno (Rev3)
  Module_2 = Adafruit Motor/Stepper/Servo Shield [part_number="Adafruit #1438"]
  U1 = WS2812 RGB LED matrix 4x4
  R1 = Resistor [tolerance=±5% resistance=220 package="1206 [SMD]"]
  M2 = DC Motor
  M1 = DC Motor
  R2 = Resistor [tolerance=±5% resistance=220 package="1206 [SMD]"]
  LED1 = smd LED [color="Red (633nm)" package="0805 [SMD]"]
  J1 = Basic Servo
  U2 = WS2812 RGB LED matrix 4x4

nets:
  N1: Module_1.A0, Module_2.AD0, R1.Pin_1
  N2: Module_1.A1, Module_2.AD1
  N3: Module_1.A2, Module_2.AD2
  N4: Module_1.A3, Module_2.AD3
  N5: Module_1.A4/SDA, Module_2.AD4/SDA
  N6: Module_1.A5/SCL, Module_2.AD5/SCL
  N7: Module_1.D8, Module_2.D8
  N8: Module_1.D9_PWM, Module_2.D9
  N9: Module_1.D10_PWM/SS, Module_2.D10, J1.pulse
  N10: Module_1.D11_PWM/MOSI, Module_2.D11
  N11: Module_1.D12/MISO, Module_2.D12
  N12: Module_1.D2, Module_2.D2, LED1.anode
  N13: Module_1.D3_PWM, Module_2.D3
  N14: Module_1.D4, Module_2.D4
  N15: Module_1.D5_PWM, Module_2.D5
  N16: Module_1.D6_PWM, Module_2.D6
  N17: Module_1.D7, Module_2.D7
  5V: Module_1.5V, Module_2.+5V, U1.VCC#1, J1.vcc
  GND: Module_1.GND, Module_2.GND, U1.GND#0, U1.GND#3, R2.Pin_1, J1.gnd
  N18: Module_2.M2A, M2.pin_2
  N19: Module_2.M2B, M2.pin_1
  N20: Module_2.M1B, M1.pin_2
  N21: Module_2.M1A, M1.pin_1
  N22: U1.DIN, R1.Pin_0
  N23: U1.GND#4, U1.GND#7, U2.GND
  N24: U1.VCC#5, U2.VCC
  N25: U1.DOUT, U2.DIN
  N26: R2.Pin_0, LED1.cathode

custom parts:
  Adafruit Motor/Stepper/Servo Shield: The original Adafruit Motorshield kit is one of our most beloved kits, which is why we decided to make something even better. We have upgraded the shield kit to make the bestest, easiest way to drive DC and Stepper motors. This shield will make quick work of your next robotics project! We kept the ability to drive up to 4 DC motors or 2 stepper motors, but added many improvements: Instead of a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
  WS2812 RGB LED matrix 4x4: WS2812 matrix 4x4
